# Fritzing sketch Circuito Desafio (saved by Fritzing 0.9.2b)
circuit board: 8.46667cm x 5.64444cm
breadboards: 1

parts:
  Parte1 = Arduino Uno (Rev3)
  J1 = Basic Servo
  J2 = Basic Servo
  J3 = Infrared Proximity Sensor
  U1 = LCD-16X2 [package=lcd-8x2-kit]

nets:
  N1: Parte1.D9_PWM, U1.VO
  N2: Parte1.D11_PWM/MOSI, U1.E
  N3: Parte1.D12/MISO, U1.RS
  N4: Parte1.D13/SCK, J1.pulse
  GND: Parte1.GND, J1.gnd, J2.gnd, J3.GND, U1.VSS
  N5: Parte1.D2, U1.DB7
  N6: Parte1.D3_PWM, U1.DB6
  N7: Parte1.D4, U1.DB5
  N8: Parte1.D5_PWM, U1.DB4
  N9: Parte1.D7, J2.pulse
  VCC: Parte1.5V, J1.vcc, J2.vcc, J3.Vcc, U1.VDD

notes:
  Circuito del Disp
  Ard/Disp/Color
  2/14/Naranja
  3/13/Amarillo
  4/12/Verde
  5/11/Azul
  9/3Morado
  11/6/Gris
  12/4/Blanco
  Grd/1/Marron
  5V/2/Rojo
  Grd/5/Negro
