# Fritzing sketch Circuito aparentemente completo Desafio (saved by Fritzing 0.9.2b)
perfboards: 2

parts:
  Parte8 = Arduino Uno (Rev3)
  U2 = ADMP504 - Ultralow Noise Microphone with Bottom Port and Analog Output [part_number=ADMP504]
  Parte9 = Ambient Light Sensor (TEMT6000 Breakout Board)
  Parte10 = Ambient Light Sensor (TEMT6000 Breakout Board)
  J4 = Infrared Proximity Sensor
  D3 = Diode [package=diode-1n4001]  # not connected
  J5 = Basic Servo
  J6 = Basic Servo
  LED3 = LED - 5mm [color="Red (633nm)" package="5 mm [THT]"]  # not connected
  LED4 = LED - 5mm [color="Red (633nm)" package="5 mm [THT]"]  # not connected
  M7 = DC Motor  # not connected
  M8 = DC Motor  # not connected
  VCC3 = Battery block 9V
  VCC4 = Battery block 9V
  R3 = Resistor [tolerance=±5% resistance=220 package=THT]
  R4 = Resistor [tolerance=±5% resistance=220 package=THT]
  Parte12 = Compass Module - HMC6352

nets:
  N1: Parte8.A1, Parte12.VCC
  N2: Parte8.A2, U2.OUTPUT
  N3: Parte8.A3, U2.GND
  N4: Parte8.A4/SDA, R4.Pin_1
  N5: Parte8.A5/SCL, R3.Pin_1
  N6: Parte8.D8, J4.Vout
  N7: Parte8.D9_PWM, Parte10.VCC
  N8: Parte8.D10_PWM/SS, J6.pulse
  N9: Parte8.D2, Parte9.VCC
  N10: Parte8.D6_PWM, J5.pulse
  5V: Parte8.5V, J4.Vcc
  N11: Parte8.VIN, VCC4.+
  N12: J4.GND, VCC4.-
  N13: VCC3.-, Parte12.SDA
  N14: VCC3.+, Parte12.GND

notes:
  Relay
  15V
