# Fritzing sketch Comienzo Desafio (saved by Fritzing 0.9.2b)
breadboards: 1

parts:
  J1 = Basic Servo
  LED1 = LED - 5mm [color="Red (633nm)" package="5 mm [THT]"]  # not connected
  LED2 = LED - 5mm [color="Red (633nm)" package="5 mm [THT]"]  # not connected
  Parte3 = Arduino Uno (Rev3)
  IC3 = L293D [package=THT]
  M5 = DC Motor
  M6 = DC Motor
  VCC1 = Battery block 9V
  VCC2 = Battery block 9V
  R1 = Resistor [tolerance=±5% resistance=220 package=THT]
  R2 = Resistor [tolerance=±5% resistance=220 package=THT]
  J2 = Basic Servo
  U1 = ADMP504 - Ultralow Noise Microphone with Bottom Port and Analog Output [part_number=ADMP504]
  Parte5 = Ambient Light Sensor (TEMT6000 Breakout Board)
  Parte6 = Ambient Light Sensor (TEMT6000 Breakout Board)
  J3 = Infrared Proximity Sensor
  D2 = Diode [package=diode-1n4001]  # not connected

nets:
  N1: J1.pulse, Parte3.D10_PWM/SS
  N2: Parte3.A2, U1.OUTPUT
  N3: Parte3.A3, U1.GND
  N4: Parte3.A4/SDA, R2.Pin_1
  N5: Parte3.A5/SCL, R1.Pin_1
  N6: Parte3.D8, J3.Vout
  N7: Parte3.D9_PWM, Parte5.VCC
  N8: Parte3.D11_PWM/MOSI, IC3.In_4
  N9: Parte3.D12/MISO, IC3.In_3
  N10: Parte3.D13/SCK, IC3.Enable_2
  N11: Parte3.D2, Parte6.VCC
  N12: Parte3.D3_PWM, IC3.In_1
  N13: Parte3.D4, IC3.In_2
  N14: Parte3.D5_PWM, IC3.Enable_1
  N15: Parte3.D6_PWM, J2.pulse
  5V: Parte3.5V, J3.Vcc
  N16: Parte3.VIN, VCC2.+
  N17: IC3.Out_1_(_Controlled_by_Enable_1_), M6.pin_2
  N18: IC3.0V, VCC1.-
  N19: IC3.Out_2_(_Controlled_by_Enable_1_), M6.pin_1
  N20: IC3.+Vmotor, IC3.+V
  N21: IC3.Out_3_(_Controlled_by_Enable_2_), M5.pin_2
  N22: IC3.Out_4_(_Controlled_by_Enable_2_), M5.pin_1
  N23: VCC2.-, J3.GND
